// Logisim project processador_vetorial.circ as structural Verilog
module breg (
  input  [7:0] D,
  input  W,
  input  [1:0] RD,
  input  CLK,
  input  [1:0] RS1,
  input  [1:0] RS2,
  output [7:0] A,
  output [7:0] B
);

  wire W1, W2, W3, W4;
  wire [7:0] VR1, VR2, VR3, VR4;

  Demultiplexer #(.select(2)) demultiplexer_1 (.out0(W1), .out1(W2), .out2(W3), .out3(W4), .in(W), .sel(RD));
  Register register_1 (.D(D), .en(W1), .clk(CLK), .Q(VR1));  // open: clr
  Register register_2 (.D(D), .en(W2), .clk(CLK), .Q(VR2));  // open: clr
  Register register_3 (.D(D), .en(W3), .clk(CLK), .Q(VR3));  // open: clr
  Register register_4 (.D(D), .en(W4), .clk(CLK), .Q(VR4));  // open: clr
  Multiplexer #(.select(2), .width(8)) multiplexer_1 (.in0(VR1), .in1(VR2), .in2(VR3), .in3(VR4), .out(A), .sel(RS1));
  Multiplexer #(.select(2), .width(8)) multiplexer_2 (.in0(VR1), .in1(VR2), .in2(VR3), .in3(VR4), .out(B), .sel(RS2));

  // Other names for the same wires on the sheet: DADO[7:0] = D
endmodule

module ULA (
  input  [7:0] A,
  input  [7:0] B,
  input  [1:0] OPULA,
  output [7:0] C
);

  wire [7:0] adder_1_out, and_1_out, subtractor_1_out;

  Adder adder_1 (.a(A), .b(B), .out(adder_1_out));  // open: cin, cout
  Subtractor subtractor_1 (.a(A), .b(B), .out(subtractor_1_out));  // open: bin, bout
  assign and_1_out = A & B;  // AND_Gate and_1, 8 bits wide
  Multiplexer #(.select(2), .width(8)) multiplexer_1 (
    .in0(adder_1_out), .in1(subtractor_1_out), .in2(and_1_out), .out(C), .sel(OPULA));  // open: in3
endmodule

module breg_vet0 (
  input  [7:0] D,
  input  W,
  input  [1:0] RD,
  input  CLK,
  input  [1:0] RS1,
  input  [1:0] RS2,
  output [7:0] A,
  output [7:0] B
);

  wire W2, W3, W4;
  wire [7:0] VR2, VR3, VR4;

  Demultiplexer #(.select(2)) demultiplexer_1 (.out1(W2), .out2(W3), .out3(W4), .in(W), .sel(RD));  // open: out0
  Register register_1 (.D(D), .en(W2), .clk(CLK), .Q(VR2));  // open: clr
  Register register_2 (.D(D), .en(W3), .clk(CLK), .Q(VR3));  // open: clr
  Register register_3 (.D(D), .en(W4), .clk(CLK), .Q(VR4));  // open: clr
  Multiplexer #(.select(2), .width(8)) multiplexer_1 (
    .in0({8{1'b0}}), .in1(VR2), .in2(VR3), .in3(VR4), .out(A), .sel(RS1));
  Multiplexer #(.select(2), .width(8)) multiplexer_2 (
    .in0({8{1'b0}}), .in1(VR2), .in2(VR3), .in3(VR4), .out(B), .sel(RS2));

  // Other names for the same wires on the sheet: DADO[7:0] = D
endmodule

module breg_vet1 (
  input  [7:0] D,
  input  W,
  input  [1:0] RD,
  input  CLK,
  input  [1:0] RS1,
  input  [1:0] RS2,
  output [7:0] A,
  output [7:0] B
);

  wire W2, W3, W4;
  wire [7:0] VR2, VR3, VR4;

  Demultiplexer #(.select(2)) demultiplexer_1 (.out1(W2), .out2(W3), .out3(W4), .in(W), .sel(RD));  // open: out0
  Register register_1 (.D(D), .en(W2), .clk(CLK), .Q(VR2));  // open: clr
  Register register_2 (.D(D), .en(W3), .clk(CLK), .Q(VR3));  // open: clr
  Register register_3 (.D(D), .en(W4), .clk(CLK), .Q(VR4));  // open: clr
  Multiplexer #(.select(2), .width(8)) multiplexer_1 (.in0(8'h1), .in1(VR2), .in2(VR3), .in3(VR4), .out(A), .sel(RS1));
  Multiplexer #(.select(2), .width(8)) multiplexer_2 (.in0(8'h1), .in1(VR2), .in2(VR3), .in3(VR4), .out(B), .sel(RS2));

  // Other names for the same wires on the sheet: DADO[7:0] = D
endmodule

module breg_vet2 (
  input  [7:0] D,
  input  W,
  input  [1:0] RD,
  input  CLK,
  input  [1:0] RS1,
  input  [1:0] RS2,
  output [7:0] A,
  output [7:0] B
);

  wire W2, W3, W4;
  wire [7:0] VR2, VR3, VR4;

  Demultiplexer #(.select(2)) demultiplexer_1 (.out1(W2), .out2(W3), .out3(W4), .in(W), .sel(RD));  // open: out0
  Register register_1 (.D(D), .en(W2), .clk(CLK), .Q(VR2));  // open: clr
  Register register_2 (.D(D), .en(W3), .clk(CLK), .Q(VR3));  // open: clr
  Register register_3 (.D(D), .en(W4), .clk(CLK), .Q(VR4));  // open: clr
  Multiplexer #(.select(2), .width(8)) multiplexer_1 (.in0(8'h2), .in1(VR2), .in2(VR3), .in3(VR4), .out(A), .sel(RS1));
  Multiplexer #(.select(2), .width(8)) multiplexer_2 (.in0(8'h2), .in1(VR2), .in2(VR3), .in3(VR4), .out(B), .sel(RS2));

  // Other names for the same wires on the sheet: DADO[7:0] = D
endmodule

module breg_vet3 (
  input  [7:0] D,
  input  W,
  input  [1:0] RD,
  input  CLK,
  input  [1:0] RS1,
  input  [1:0] RS2,
  output [7:0] A,
  output [7:0] B
);

  wire W2, W3, W4;
  wire [7:0] VR2, VR3, VR4;

  Demultiplexer #(.select(2)) demultiplexer_1 (.out1(W2), .out2(W3), .out3(W4), .in(W), .sel(RD));  // open: out0
  Register register_1 (.D(D), .en(W2), .clk(CLK), .Q(VR2));  // open: clr
  Register register_2 (.D(D), .en(W3), .clk(CLK), .Q(VR3));  // open: clr
  Register register_3 (.D(D), .en(W4), .clk(CLK), .Q(VR4));  // open: clr
  Multiplexer #(.select(2), .width(8)) multiplexer_1 (.in0(8'h3), .in1(VR2), .in2(VR3), .in3(VR4), .out(A), .sel(RS1));
  Multiplexer #(.select(2), .width(8)) multiplexer_2 (.in0(8'h3), .in1(VR2), .in2(VR3), .in3(VR4), .out(B), .sel(RS2));

  // Other names for the same wires on the sheet: DADO[7:0] = D
endmodule
