// Logisim project processador_viw.circ as structural Verilog: 10 circuits, main circuit main
module main (
);

  wire MemRead, MemWrite, MuxL1Src, RegWriteL1, RegWriteL3, RegWriteL4, Sig_BNZR, Sig_BRZI, Sig_BRZR, Sig_JR,
       undriven, undriven_2;
  wire [1:0] RaLn1, RaLn2, RaLn3, RaLn4, RbLn1, RbLn2, RbLn3, RbLn4;
  wire [2:0] control_1_opula1, control_1_opula2;
  wire [7:0] breg_1_oaln1, breg_1_oaln3, breg_1_oaln4, breg_1_obln1, breg_1_obln3, breg_1_obln4, DadoL3,
       DadoL4, move_1_movh, move_1_movl;
  wire [31:4] dualram_1_p1;

  // DualRAM #(.dataWidth(32)) dualram_1: pin names not known; wires that end beside it: {dualram_1_p1[31:28], RaLn1, RbLn1, dualram_1_p1[23:20], RaLn2, RbLn2, dualram_1_p1[15:12], RaLn3, RbLn3, dualram_1_p1[7:4], RaLn4, RbLn4}
  Breg breg_1 (
    .DataL3(DadoL3), .DataL4(DadoL4), .RegWriteLn1(RegWriteL1), .clock(undriven_2), .RegWriteLn3(RegWriteL3),
    .RegWriteLn4(RegWriteL4), .reset(undriven), .RaLn1(RaLn1), .RbLn1(RbLn1), .RaLn2(RaLn2), .RbLn2(RbLn2),
    .RaLn3(RaLn3), .RbLn3(RbLn3), .RaLn4(RaLn4), .RbLn4(RbLn4), .OALn1(breg_1_oaln1), .OBLn1(breg_1_obln1),
    .OALn3(breg_1_oaln3), .OBLn3(breg_1_obln3), .OALn4(breg_1_oaln4), .OBLn4(breg_1_obln4));  // open: DataL1, OALn2, OBLn2
  control control_1 (
    .InstrL1(dualram_1_p1[31:28]), .InstrL2(dualram_1_p1[23:20]), .InstrL3(dualram_1_p1[15:12]),
    .InstrL4(dualram_1_p1[7:4]), .MemWriteL1(MemWrite), .MemrRead(MemRead), .MuxL1Src(MuxL1Src),
    .RegWriteL1(RegWriteL1), .Sig_BRZR(Sig_BRZR), .Sig_BRZI(Sig_BRZI), .Sig_JR(Sig_JR), .Sig_BNZR(Sig_BNZR),
    .RegWriteL3(RegWriteL3), .OpULA1(control_1_opula1), .RegWriteL4(RegWriteL4), .OpULA2(control_1_opula2));
  move move_1 (.r0(breg_1_oaln1), .movH(move_1_movh), .movL(move_1_movl));  // open: imm
  ula L3 (.entradaA(breg_1_oaln3), .entradaB(breg_1_obln3), .OpULA(control_1_opula1), .saidaULA(DadoL3));
  ula L4 (.entradaA(breg_1_oaln4), .entradaB(breg_1_obln4), .OpULA(control_1_opula2), .saidaULA(DadoL4));
endmodule

module ula (
  input  [7:0] entradaA,
  input  [7:0] entradaB,
  input  [2:0] OpULA,
  output [7:0] saidaULA
);

  wire nor_1_out, or_2_out;
  wire [7:0] adder_1_out, adder_2_out, bit_extender_1_out, multiplexer_1_out, multiplexer_2_out, or_1_out,
       shifter_1_out, shifter_2_out, subtractor_1_out;

  Adder adder_1 (.a(entradaA), .b(entradaB), .out(adder_1_out));  // open: cin, cout
  Subtractor subtractor_1 (.a(entradaA), .b(entradaB), .out(subtractor_1_out));  // open: bin, bout
  assign or_1_out = entradaA | entradaB;  // OR_Gate or_1, 8 bits wide
  Shifter shifter_1 (.in(entradaA), .\dist (entradaB[2:0]), .out(shifter_1_out));
  or or_2 (or_2_out, entradaB[3], entradaB[4], entradaB[5], entradaB[6], entradaB[7]);
  Shifter #(.shift("lr")) shifter_2 (.in(entradaA), .\dist (entradaB[2:0]), .out(shifter_2_out));
  Adder adder_2 (.a(entradaA), .b(8'h1), .out(adder_2_out));  // open: cin, cout
  nor nor_1 (nor_1_out, entradaB[0], entradaB[1], entradaB[2], entradaB[3], entradaB[4], entradaB[5], entradaB[6], entradaB[7]);
  Multiplexer #(.width(8)) multiplexer_1 (
    .in0(shifter_1_out), .in1({8{1'b0}}), .out(multiplexer_1_out), .sel(or_2_out));
  Multiplexer #(.width(8)) multiplexer_2 (
    .in0({8{1'b0}}), .in1(shifter_2_out), .out(multiplexer_2_out), .sel(or_2_out));
  assign bit_extender_1_out = {{7{nor_1_out}}, nor_1_out};  // Bit_Extender bit_extender_1
  Multiplexer #(.select(3), .width(8)) multiplexer_3 (
    .in0(adder_1_out), .in1(subtractor_1_out), .in2(adder_2_out), .in3(or_1_out), .in4(bit_extender_1_out),
    .in5(multiplexer_1_out), .in6(multiplexer_2_out), .out(saidaULA), .sel(OpULA));  // open: in7
endmodule

module Breg (
  input  [7:0] DataL1,
  input  [7:0] DataL3,
  input  [7:0] DataL4,
  input  RegWriteLn1,
  input  clock,
  input  RegWriteLn3,
  input  RegWriteLn4,
  input  reset,
  input  [1:0] RaLn1,
  input  [1:0] RbLn1,
  input  [1:0] RaLn2,
  input  [1:0] RbLn2,
  input  [1:0] RaLn3,
  input  [1:0] RbLn3,
  input  [1:0] RaLn4,
  input  [1:0] RbLn4,
  output [7:0] OALn1,
  output [7:0] OBLn1,
  output [7:0] OALn2,
  output [7:0] OBLn2,
  output [7:0] OALn3,
  output [7:0] OBLn3,
  output [7:0] OALn4,
  output [7:0] OBLn4
);

  wire demultiplexer_4_out0, demultiplexer_4_out1, demultiplexer_4_out2, demultiplexer_4_out3,
       demultiplexer_5_out0, demultiplexer_5_out1, demultiplexer_5_out2, demultiplexer_5_out3,
       demultiplexer_6_out0, demultiplexer_6_out1, demultiplexer_6_out2, demultiplexer_6_out3, or_1_out,
       or_3_out, or_6_out, or_8_out;
  wire [1:0] RegALn1, RegALn3, RegALn4;
  wire [7:0] demultiplexer_1_out0, demultiplexer_1_out1, demultiplexer_1_out2, demultiplexer_1_out3,
       demultiplexer_2_out0, demultiplexer_2_out1, demultiplexer_2_out2, demultiplexer_2_out3,
       demultiplexer_3_out0, demultiplexer_3_out1, demultiplexer_3_out2, demultiplexer_3_out3,
       multiplexer_1_out, multiplexer_2_out, multiplexer_3_out, or_2_out, or_4_out, or_5_out, or_7_out, R0_q,
       R1_q, R2_q, R3_q;

  Multiplexer #(.width(8)) multiplexer_1 (.in0({8{1'b0}}), .in1(DataL1), .out(multiplexer_1_out), .sel(RegWriteLn1));
  Demultiplexer #(.select(2), .width(8)) demultiplexer_1 (
    .out0(demultiplexer_1_out0), .out1(demultiplexer_1_out1), .out2(demultiplexer_1_out2),
    .out3(demultiplexer_1_out3), .in(multiplexer_1_out), .sel(RegALn1));
  Multiplexer #(.width(8)) multiplexer_2 (.in0({8{1'b0}}), .in1(DataL3), .out(multiplexer_2_out), .sel(RegWriteLn3));
  Demultiplexer #(.select(2), .width(8)) demultiplexer_2 (
    .out0(demultiplexer_2_out0), .out1(demultiplexer_2_out1), .out2(demultiplexer_2_out2),
    .out3(demultiplexer_2_out3), .in(multiplexer_2_out), .sel(RegALn3));
  Multiplexer #(.width(8)) multiplexer_3 (.in0({8{1'b0}}), .in1(DataL4), .out(multiplexer_3_out), .sel(RegWriteLn4));
  Demultiplexer #(.select(2), .width(8)) demultiplexer_3 (
    .out0(demultiplexer_3_out0), .out1(demultiplexer_3_out1), .out2(demultiplexer_3_out2),
    .out3(demultiplexer_3_out3), .in(multiplexer_3_out), .sel(RegALn4));
  Demultiplexer #(.select(2)) demultiplexer_4 (
    .out0(demultiplexer_4_out0), .out1(demultiplexer_4_out1), .out2(demultiplexer_4_out2),
    .out3(demultiplexer_4_out3), .in(RegWriteLn1), .sel(RegALn1));
  Demultiplexer #(.select(2)) demultiplexer_5 (
    .out0(demultiplexer_5_out0), .out1(demultiplexer_5_out1), .out2(demultiplexer_5_out2),
    .out3(demultiplexer_5_out3), .in(RegWriteLn3), .sel(RegALn3));
  Demultiplexer #(.select(2)) demultiplexer_6 (
    .out0(demultiplexer_6_out0), .out1(demultiplexer_6_out1), .out2(demultiplexer_6_out2),
    .out3(demultiplexer_6_out3), .in(RegWriteLn4), .sel(RegALn4));
  or or_1 (or_1_out, demultiplexer_4_out0, demultiplexer_5_out0, demultiplexer_6_out0);
  assign or_2_out = demultiplexer_1_out1 | demultiplexer_2_out1 | demultiplexer_3_out1;  // OR_Gate or_2, 8 bits wide
  or or_3 (or_3_out, demultiplexer_4_out1, demultiplexer_5_out1, demultiplexer_6_out1);
  assign or_4_out = demultiplexer_1_out2 | demultiplexer_2_out2 | demultiplexer_3_out2;  // OR_Gate or_4, 8 bits wide
  assign or_5_out = demultiplexer_3_out0 | demultiplexer_2_out0 | demultiplexer_1_out0;  // OR_Gate or_5, 8 bits wide
  or or_6 (or_6_out, demultiplexer_4_out2, demultiplexer_5_out2, demultiplexer_6_out2);
  assign or_7_out = demultiplexer_1_out3 | demultiplexer_2_out3 | demultiplexer_3_out3;  // OR_Gate or_7, 8 bits wide
  or or_8 (or_8_out, demultiplexer_4_out3, demultiplexer_5_out3, demultiplexer_6_out3);
  Register R0 (.D(or_5_out), .en(or_1_out), .clk(reset), .Q(R0_q), .clr(clock));
  Register R1 (.D(or_2_out), .en(or_3_out), .clk(reset), .Q(R1_q), .clr(clock));
  Register R2 (.D(or_4_out), .en(or_6_out), .clk(reset), .Q(R2_q), .clr(clock));
  Register R3 (.D(or_7_out), .en(or_8_out), .clk(reset), .Q(R3_q), .clr(clock));
  Multiplexer #(.select(2), .width(8)) multiplexer_4 (
    .in0(R0_q), .in1(R1_q), .in2(R2_q), .in3(R3_q), .out(OALn1), .sel(RaLn1));
  Multiplexer #(.select(2), .width(8)) multiplexer_5 (
    .in0(R0_q), .in1(R1_q), .in2(R2_q), .in3(R3_q), .out(OBLn1), .sel(RbLn1));
  Multiplexer #(.select(2), .width(8)) multiplexer_6 (
    .in0(R0_q), .in1(R1_q), .in2(R2_q), .in3(R3_q), .out(OALn2), .sel(RaLn2));
  Multiplexer #(.select(2), .width(8)) multiplexer_7 (
    .in0(R0_q), .in1(R1_q), .in2(R2_q), .in3(R3_q), .out(OBLn2), .sel(RbLn2));
  Multiplexer #(.select(2), .width(8)) multiplexer_8 (
    .in0(R0_q), .in1(R1_q), .in2(R2_q), .in3(R3_q), .out(OALn3), .sel(RaLn3));
  Multiplexer #(.select(2), .width(8)) multiplexer_9 (
    .in0(R0_q), .in1(R1_q), .in2(R2_q), .in3(R3_q), .out(OBLn3), .sel(RbLn3));
  Multiplexer #(.select(2), .width(8)) multiplexer_10 (
    .in0(R0_q), .in1(R1_q), .in2(R2_q), .in3(R3_q), .out(OALn4), .sel(RaLn4));
  Multiplexer #(.select(2), .width(8)) multiplexer_11 (
    .in0(R0_q), .in1(R1_q), .in2(R2_q), .in3(R3_q), .out(OBLn4), .sel(RbLn4));
endmodule

module control (
  input  [3:0] InstrL1,
  input  [3:0] InstrL2,
  input  [3:0] InstrL3,
  input  [3:0] InstrL4,
  output MemWriteL1,
  output MemrRead,
  output MuxL1Src,
  output RegWriteL1,
  output Sig_BRZR,
  output Sig_BRZI,
  output Sig_JR,
  output Sig_BNZR,
  output RegWriteL3,
  output [2:0] OpULA1,
  output RegWriteL4,
  output [2:0] OpULA2
);

  controlL1 controll1_1 (
    .Op3(InstrL1[3]), .Op2(InstrL1[2]), .Op1(InstrL1[1]), .Op0(InstrL1[0]), .MemWriteL1(MemWriteL1),
    .MemRead(MemrRead), .MuxL1Src(MuxL1Src), .RegWriteL1(RegWriteL1));
  controlL2 controll2_1 (
    .Op3(InstrL2[0]), .Op2(InstrL2[1]), .Op1(InstrL2[2]), .Op0(InstrL2[3]), .Sig_BRZR(Sig_BRZR),
    .Sig_BRZI(Sig_BRZI), .Sig_JR(Sig_JR), .Sig_BNZR(Sig_BNZR));
  controlL3L4 controll3l4_1 (
    .ULA1(InstrL3), .ULA2(InstrL4), .RegWriteULA1(RegWriteL3), .OpULA1(OpULA1), .RegWriteULA2(RegWriteL4),
    .OpULA2(OpULA2));
endmodule

module move (
  input  [7:0] r0,
  input  [3:0] imm,
  output [7:0] movH,
  output [7:0] movL
);


  assign movH = r0;
  assign movL = {r0[7:4], imm};
endmodule

module mem (
);

  // DualRAM dualram_1: pin names not known
endmodule

module controlL1 (
  input  Op3,
  input  Op2,
  input  Op1,
  input  Op0,
  output MemWriteL1,
  output MemRead,
  output MuxL1Src,
  output RegWriteL1
);

  wire and_4_out, and_5_out, not_1_out, not_2_out, not_3_out;

  not not_1 (not_1_out, Op3);
  not not_2 (not_2_out, Op1);
  not not_3 (not_3_out, Op0);
  and and_1 (MemWriteL1, not_1_out, Op2, not_2_out, Op0);
  and and_2 (MemRead, not_1_out, Op2, not_2_out, not_3_out);
  and and_3 (MuxL1Src, not_1_out, Op2, Op1);
  and and_4 (and_4_out, not_1_out, Op2, not_3_out);
  and and_5 (and_5_out, not_1_out, Op2, Op1);
  or or_1 (RegWriteL1, and_4_out, and_5_out);
endmodule

module controlL2 (
  input  Op3,
  input  Op2,
  input  Op1,
  input  Op0,
  output Sig_BRZR,
  output Sig_BRZI,
  output Sig_JR,
  output Sig_BNZR
);

  wire not_1_out, not_2_out, not_3_out, not_4_out;

  not not_1 (not_1_out, Op3);
  not not_2 (not_2_out, Op2);
  not not_3 (not_3_out, Op1);
  not not_4 (not_4_out, Op0);
  and and_1 (Sig_BRZR, not_1_out, not_2_out, not_3_out, not_4_out);
  and and_2 (Sig_BRZI, not_1_out, not_2_out, not_3_out, Op0);
  and and_3 (Sig_JR, not_1_out, not_2_out, Op1, not_4_out);
  and and_4 (Sig_BNZR, not_1_out, not_2_out, Op1, Op0);
endmodule

module controlL3L4 (
  input  [3:0] ULA1,
  input  [3:0] ULA2,
  output RegWriteULA1,
  output [2:0] OpULA1,
  output RegWriteULA2,
  output [2:0] OpULA2
);

  wire nand_1_out, nand_2_out;

  nand nand_1 (nand_1_out, ULA1[0], ULA1[1], ULA1[2]);
  nand nand_2 (nand_2_out, ULA2[0], ULA2[1], ULA2[2]);
  and and_1 (RegWriteULA1, nand_1_out, ULA1[3]);
  and and_2 (RegWriteULA2, nand_2_out, ULA2[3]);
  Multiplexer #(.width(3)) multiplexer_1 (.in0(3'b000), .in1(ULA2[2:0]), .out(OpULA2), .sel(RegWriteULA2));
  Multiplexer #(.width(3)) multiplexer_2 (.in0(3'b000), .in1(ULA1[2:0]), .out(OpULA1), .sel(RegWriteULA1));
endmodule

module zero (
  input  [7:0] in_1,
  output iszero
);

  nor nor_1 (iszero, in_1[0], in_1[1], in_1[2], in_1[3], in_1[4], in_1[5], in_1[6], in_1[7]);
endmodule
